// Logisim project ControlUnit.circ as structural Verilog: 1 circuit, main circuit Control Unit
module Control_Unit (
  input  PCOverflow,
  input  [19:0] Inst,
  input  clk,
  output Fetch,
  output ALU_Control,
  output RegRead,
  output RegWrite,
  output MemRead,
  output MemWrite,
  output PCRead,
  output PCWrite,
  output Imm,
  output BE_Select,
  output [2:0] ALU_Select,
  output [3:0] Dr,
  output [3:0] Sr1,
  output [3:0] Sr2,
  output [19:0] Imm_Offset,
  output [9:0] Addr
);

  wire Instruction_Decoder_alu, Instruction_Decoder_be, Instruction_Decoder_halt, Instruction_Decoder_jump,
       Instruction_Decoder_ld, Instruction_Decoder_pop, Instruction_Decoder_push, Instruction_Decoder_st,
       not_1_out, signal_generator_1_p12, signal_generator_1_p14, state_manager_1_s0, state_manager_1_s1,
       state_manager_1_s2, terminator_1_halted;
  wire [19:0] IR_q;

  _20BitRegister IR (.clk(signal_generator_1_p14), .I(Inst), .Q(IR_q), .W_Enable(not_1_out));
  not not_1 (not_1_out, signal_generator_1_p14);
  Instruction_Decoder Instruction_Decoder (
    .in_1(IR_q), .ALU_Select(ALU_Select), .ALU(Instruction_Decoder_alu), .IMM(Imm),
    .LD(Instruction_Decoder_ld), .ST(Instruction_Decoder_st), .PUSH(Instruction_Decoder_push),
    .POP(Instruction_Decoder_pop), .JUMP(Instruction_Decoder_jump), .BE(Instruction_Decoder_be),
    .BE_Select(BE_Select), .HALT(Instruction_Decoder_halt), .DR(Dr), .SR1(Sr1), .SR2(Sr2),
    .IMM_2(Imm_Offset), .ADDR(Addr));
  State_Manager state_manager_1 (
    .ALU(Instruction_Decoder_alu), .LD(Instruction_Decoder_ld), .ST(Instruction_Decoder_st),
    .PUSH(Instruction_Decoder_push), .POP(Instruction_Decoder_pop), .JUMP(Instruction_Decoder_jump),
    .BE(Instruction_Decoder_be), .clk(clk), .S2(state_manager_1_s2), .S1(state_manager_1_s1),
    .S0(state_manager_1_s0));
  Terminator terminator_1 (
    .clk(clk), .Decode(signal_generator_1_p14), .Halt_Instruction(Instruction_Decoder_halt),
    .Instruction_End(signal_generator_1_p12), .PC_Overflow(PCOverflow), .Halted(terminator_1_halted));
  // Signal_Generator signal_generator_1: pin names not known; wires that end beside it: terminator_1_halted, Instruction_Decoder_alu, Instruction_Decoder_ld, Instruction_Decoder_st, Instruction_Decoder_push, Instruction_Decoder_pop, Instruction_Decoder_jump, Instruction_Decoder_be, state_manager_1_s2, state_manager_1_s1, state_manager_1_s0, signal_generator_1_p12, Fetch, signal_generator_1_p14, ALU_Control, RegRead, RegWrite, MemRead, MemWrite, PCRead, PCWrite

  // Notes on the sheet:
  //   Inst: pull=down
  //   clk: pull=down
  //   BE_Select: pull=down
  //   RegRead: pull=down
  //   ALU_Select: pull=down
  //   Addr: pull=down
  //   Dr: pull=down
  //   Imm_Offset: pull=down
  //   Sr1: pull=down
  //   Fetch: pull=down
  //   PCOverflow: pull=down
  //   MemRead: pull=down
  //   ALU_Control: pull=down
  //   PCRead: pull=down
  //   RegWrite: pull=down
  //   MemWrite: pull=down
  //   Imm: pull=down
  //   Sr2: pull=down
  //   PCWrite: pull=down
endmodule
