// Logisim project RegisterFile.circ as structural Verilog: 1 circuit, main circuit RegisterFile
module RegisterFile (
  input  [19:0] WR0,
  input  [19:0] WR1,
  input  [19:0] WR2,
  input  [19:0] WR3,
  input  [19:0] WR4,
  input  [19:0] WR5,
  input  [19:0] WR6,
  input  [19:0] WR7,
  input  [19:0] WR8,
  input  [19:0] WR9,
  input  [19:0] WR10,
  input  [19:0] WR11,
  input  [19:0] WR12,
  input  [19:0] WR13,
  input  [19:0] WR14,
  input  [19:0] WR15,
  input  C,
  output [19:0] RR0,
  output [19:0] RR1,
  output [19:0] RR2,
  output [19:0] RR3,
  output [19:0] RR4,
  output [19:0] RR5,
  output [19:0] RR6,
  output [19:0] RR7,
  output [19:0] RR8,
  output [19:0] RR9,
  output [19:0] RR10,
  output [19:0] RR11,
  output [19:0] RR12,
  output [19:0] RR13,
  output [19:0] RR14,
  output [19:0] RR15
);

  _20BitRegister R0 (.C(C), .I(WR0), .Q(RR0));
  _20BitRegister R1 (.C(C), .I(WR1), .Q(RR1));
  _20BitRegister R2 (.C(C), .I(WR2), .Q(RR2));
  _20BitRegister R3 (.C(C), .I(WR3), .Q(RR3));
  _20BitRegister R4 (.C(C), .I(WR4), .Q(RR4));
  _20BitRegister R5 (.C(C), .I(WR5), .Q(RR5));
  _20BitRegister R6 (.C(C), .I(WR6), .Q(RR6));
  _20BitRegister R7 (.C(C), .I(WR7), .Q(RR7));
  _20BitRegister R8 (.C(C), .I(WR8), .Q(RR8));
  _20BitRegister R9 (.C(C), .I(WR9), .Q(RR9));
  _20BitRegister R10 (.C(C), .I(WR10), .Q(RR10));
  _20BitRegister R11 (.C(C), .I(WR11), .Q(RR11));
  _20BitRegister R12 (.C(C), .I(WR12), .Q(RR12));
  _20BitRegister R13 (.C(C), .I(WR13), .Q(RR13));
  _20BitRegister R14 (.C(C), .I(WR14), .Q(RR14));
  _20BitRegister R15 (.C(C), .I(WR15), .Q(RR15));
endmodule
